# Fritzing sketch Tachometer (saved by Fritzing 0.9.3b)
circuit board: 8.46667cm x 5.64444cm
breadboards: 1

parts:
  Arduino_Pro_Micro = SparkFun Pro Micro
  Hall_Sensor = KY-003 Hall Magnetic Sensor Module [package="Breakout board"]

nets:
  N1: Arduino_Pro_Micro.GND, Hall_Sensor.-
  N2: Arduino_Pro_Micro.2, Hall_Sensor.S
  VCC: Arduino_Pro_Micro.VCC, Hall_Sensor.Vin

custom parts:
  SparkFun Pro Micro: The Pro Micro is similar to the Pro Mini except with an ATmega32U4 on board. The USB transceiver inside the 32U4 allows us to add USB connectivity on-board and do away with bulky external USB interface. Based on: https://github.com/unorthodox-engineers/unorthodox-arduino/blob/master/Unorthodox/fritzing/parts/Pro%20Micro.fzpz
  KY-003 Hall Magnetic Sensor Module: KEYES KY-003 Arduino Hall Magnetic Sensor Module is a switch that will turn on/off in the presence of a magnetic field.
